# Fritzing sketch Theremin (saved by Fritzing 0.9.3b)
circuit board: 6.88566cm x 5.36311cm
breadboards: 2

parts:
  R5 = Photocell (LDR) [package=THT]
  R6 = Resistor [tolerance=±5% resistance=10k package=THT]
  PCB2 = Arduino Shield PCB  # not connected
  Arduino1 = Arduino Uno (Rev3)
  J1 = Piezo Speaker
  LED1 = RGB LED (com. cathode, rgb) [package="5 mm [THT]"]

nets:
  N1: R5.pin_0, Arduino1.5V
  N2: R5.pin_1, R6.Pin_0, Arduino1.A2
  N3: R6.Pin_1, Arduino1.GND, J1.pin1, LED1.red_anode
  N4: Arduino1.D11_PWM/MOSI, LED1.green_anode
  N5: Arduino1.D12/MISO, LED1.common_cathode
  N6: Arduino1.D13/SCK, J1.pin2, LED1.blue_anode

custom parts:
  Arduino Shield PCB: Plain PCB Shaped to fit an Arduino "Shield"
